# Fritzing sketch StarrySky (saved by Fritzing 0.9.5d)

parts:
  Arduino1 = Arduino Uno (Rev3)
  D1 = LTE-302 [package=lte-302]
  D2 = LTE-302 [package=lte-302]
  D3 = LTE-302 [package=lte-302]
  IR1 = TSOP312.., 314.. [package=THT]
  D4 = LTE-302 [package=lte-302]
  D5 = LTE-302 [package=lte-302]
  D6 = LTE-302 [package=lte-302]
  D7 = LTE-302 [package=lte-302]
  D8 = LTE-302 [package=lte-302]
  D9 = LTE-302 [package=lte-302]
  D10 = LTE-302 [package=lte-302]
  D11 = LTE-302 [package=lte-302]
  D12 = LTE-302 [package=lte-302]
  D13 = LTE-302 [package=lte-302]
  R1 = Resistor [tolerance=±5% resistance=220 package=THT]
  R2 = Resistor [tolerance=±5% resistance=220 package=THT]
  R3 = Resistor [tolerance=±5% resistance=220 package=THT]
  R4 = Resistor [tolerance=±5% resistance=220 package=THT]
  R5 = Resistor [tolerance=±5% resistance=220 package=THT]
  R7 = Resistor [tolerance=±5% resistance=220 package=THT]
  R8 = Resistor [tolerance=±5% resistance=220 package=THT]
  R9 = Resistor [tolerance=±10% resistance=220 package=THT]
  R10 = Resistor [tolerance=±5% resistance=220 package=THT]
  R16 = Resistor [tolerance=±5% resistance=220 package=THT]
  R17 = Resistor [tolerance=±5% resistance=220 package=THT]
  D14 = LTE-302 [package=lte-302]
  D15 = LTE-302 [package=lte-302]
  D16 = LTE-302 [package=lte-302]
  D17 = LTE-302 [package=lte-302]
  D18 = LTE-302 [package=lte-302]
  D19 = LTE-302 [package=lte-302]
  D20 = LTE-302 [package=lte-302]
  D21 = LTE-302 [package=lte-302]
  R18 = Resistor [tolerance=±5% resistance=220 package=THT]
  R21 = Resistor [tolerance=±5% resistance=220 package=THT]
  R25 = Resistor [tolerance=±10% resistance=220 package=THT]
  R26 = Resistor [tolerance=±5% resistance=220 package=THT]
  R27 = Resistor [tolerance=±5% resistance=220 package=THT]
  R28 = Resistor [tolerance=±5% resistance=220 package=THT]
  R29 = Resistor [tolerance=±5% resistance=220 package=THT]
  R30 = Resistor [tolerance=±5% resistance=220 package=THT]
  R32 = Resistor [tolerance=±5% resistance=220 package=THT]
  R33 = Resistor [tolerance=±5% resistance=220 package=THT]

nets:
  N1: Arduino1.D8, IR1.Data
  N2: Arduino1.D9_PWM, D1.A, D3.A, D4.A, D6.A, D7.A
  N3: Arduino1.D10_PWM/SS, D2.A, D5.A, D8.A, D9.A, D10.A, D11.A, D12.A
  GND: Arduino1.GND, IR1.GND, R1.Pin_1, R2.Pin_1, R3.Pin_1, R4.Pin_1, R5.Pin_1, R7.Pin_1, R8.Pin_1, R9.Pin_1, R10.Pin_1, R16.Pin_1, R17.Pin_1, R18.Pin_0, R21.Pin_0, R25.Pin_0, R26.Pin_0, R27.Pin_0, R28.Pin_0, R29.Pin_0, R30.Pin_1, R32.Pin_0, R33.Pin_0
  N4: Arduino1.D5_PWM, D13.A, D14.A, D15.A, D16.A, D17.A
  N5: Arduino1.D6_PWM, D18.A, D19.A, D20.A
  N6: Arduino1.5V, IR1.Vs
  N7: D1.C, R2.Pin_0
  N8: D2.C, R30.Pin_0
  N9: D3.C, R1.Pin_0
  N10: D4.C, R3.Pin_0
  N11: D5.C, R7.Pin_0
  N12: D6.C, R5.Pin_0
  N13: D7.C, R4.Pin_0
  N14: D8.C, R8.Pin_0
  N15: D9.C, R9.Pin_0
  N16: D10.C, R10.Pin_0
  N17: D11.C, R16.Pin_0
  N18: D12.C, R17.Pin_0
  N19: D13.C, R21.Pin_1
  N20: D14.C, R33.Pin_1
  N21: D15.C, R32.Pin_1
  N22: D16.C, R29.Pin_1
  N23: D17.C, R18.Pin_1
  N24: D18.C, R28.Pin_1
  N25: D19.C, R27.Pin_1
  N26: D20.C, R26.Pin_1
  N27: D21.C, R25.Pin_1
